// Logisim project 8bitPROJECT (1).circ as structural Verilog: 1 circuit, main circuit Register
module Register (
  input  [7:0] Din,
  input  in_2,
  input  in_3,
  input  in_4,
  input  in_5,
  input  Clock,
  input  Load,
  input  D1,
  input  D2,
  input  D3,
  output [7:0] out_11,
  output [7:0] out_12,
  output [7:0] out_13,
  output [7:0] out_14,
  output [7:0] B
);

  wire and_1_out, and_2_out, and_3_out, and_4_out;
  wire [7:0] and_5_out, and_6_out, and_7_out;

  and and_1 (and_1_out, in_2, Load);
  and and_2 (and_2_out, in_3, Load);
  and and_3 (and_3_out, in_4, Load);
  and and_4 (and_4_out, in_5, Load);
  Register_part D0 (.D(Din), .en(and_1_out), .Q(out_11), .clk(Clock), .clr(1'b0));
  Register_part u_D1 (.D(Din), .en(and_2_out), .Q(out_12), .clk(Clock), .clr(1'b0));
  Register_part u_D2 (.D(Din), .en(and_3_out), .Q(out_13), .clk(Clock), .clr(1'b0));
  Register_part u_D3 (.D(Din), .en(and_4_out), .Q(out_14), .clk(Clock), .clr(1'b0));
  assign and_5_out = out_14 & {8{D3}};  // AND_Gate and_5, 8 bits wide
  assign and_6_out = out_12 & {8{D1}};  // AND_Gate and_6, 8 bits wide
  assign and_7_out = out_13 & {8{D2}};  // AND_Gate and_7, 8 bits wide
  ExactlyOne xor_1[7:0] (.out(B), .in0(and_6_out), .in2(and_7_out), .in4(and_5_out));
endmodule
