// Logisim project controlunitprobably.circ as structural Verilog: 1 circuit, main circuit main
module main (
  input  [7:0] X0_C0_C1_B0_B1_F2_F1_F0,
  output D0,
  output D1,
  output D2,
  output D3,
  output D1_2,
  output D2_2,
  output D3_2,
  output F2,
  output F1,
  output F0
);

  wire demultiplexer_1_out0, demultiplexer_1_out1, demultiplexer_1_out2, demultiplexer_1_out3,
       demultiplexer_2_out1, demultiplexer_2_out2, demultiplexer_2_out3;

  Demultiplexer #(.select(2)) demultiplexer_1 (
    .out0(demultiplexer_1_out0), .out1(demultiplexer_1_out1), .out2(demultiplexer_1_out2),
    .out3(demultiplexer_1_out3), .in(1'b1), .sel(X0_C0_C1_B0_B1_F2_F1_F0[6:5]));  // open: en
  Demultiplexer #(.select(2)) demultiplexer_2 (
    .out1(demultiplexer_2_out1), .out2(demultiplexer_2_out2), .out3(demultiplexer_2_out3), .in(1'b1),
    .sel({X0_C0_C1_B0_B1_F2_F1_F0[3], X0_C0_C1_B0_B1_F2_F1_F0[4]}));  // open: out0, en
  and and_1 (F0, X0_C0_C1_B0_B1_F2_F1_F0[0], 1'b1);
  and and_2 (F1, X0_C0_C1_B0_B1_F2_F1_F0[1], 1'b1);
  and and_3 (F2, X0_C0_C1_B0_B1_F2_F1_F0[2], 1'b1);
  and and_4 (D0, demultiplexer_1_out0, 1'b1);
  and and_5 (D1, demultiplexer_1_out1, 1'b1);
  and and_6 (D2, demultiplexer_1_out2, 1'b1);
  and and_7 (D3, demultiplexer_1_out3, 1'b1);
  and and_8 (D1_2, 1'b1, demultiplexer_2_out3);
  and and_9 (D2_2, 1'b1, demultiplexer_2_out2);
  and and_10 (D3_2, 1'b1, demultiplexer_2_out1);
endmodule
