// Logisim project project1 .circ as structural Verilog: 4 circuits, main circuit 8-bit  7 seg display
module _8_bit__7_seg_display (
  input  [7:0] in_1,
  output [3:0] out_2,
  output [3:0] out_3,
  output [3:0] out_4
);

  wire dabble_1_out_5, dabble_1_out_6, dabble_1_out_7, dabble_1_out_8, dabble_2_out_5, dabble_2_out_6,
       dabble_2_out_7, dabble_2_out_8, dabble_3_out_5, dabble_3_out_6, dabble_3_out_7, dabble_3_out_8,
       dabble_5_out_5, dabble_5_out_6, dabble_5_out_7, dabble_5_out_8, dabble_7_out_5, dabble_7_out_6,
       dabble_7_out_7;

  Dabble dabble_1 (
    .in_1(in_1[5]), .in_2(in_1[6]), .in_3(in_1[7]), .in_4(1'b0), .out_5(dabble_1_out_5),
    .out_6(dabble_1_out_6), .out_7(dabble_1_out_7), .out_8(dabble_1_out_8));
  Dabble dabble_2 (
    .in_1(in_1[3]), .in_2(dabble_3_out_5), .in_3(dabble_3_out_6), .in_4(dabble_3_out_7),
    .out_5(dabble_2_out_5), .out_6(dabble_2_out_6), .out_7(dabble_2_out_7), .out_8(dabble_2_out_8));
  Dabble dabble_3 (
    .in_1(in_1[4]), .in_2(dabble_1_out_5), .in_3(dabble_1_out_6), .in_4(dabble_1_out_7),
    .out_5(dabble_3_out_5), .out_6(dabble_3_out_6), .out_7(dabble_3_out_7), .out_8(dabble_3_out_8));
  Dabble dabble_4 (
    .in_1(in_1[1]), .in_2(dabble_5_out_5), .in_3(dabble_5_out_6), .in_4(dabble_5_out_7), .out_5(out_4[1]),
    .out_6(out_4[2]), .out_7(out_4[3]), .out_8(out_3[0]));
  Dabble dabble_5 (
    .in_1(in_1[2]), .in_2(dabble_2_out_5), .in_3(dabble_2_out_6), .in_4(dabble_2_out_7),
    .out_5(dabble_5_out_5), .out_6(dabble_5_out_6), .out_7(dabble_5_out_7), .out_8(dabble_5_out_8));
  Dabble dabble_6 (
    .in_1(dabble_5_out_8), .in_2(dabble_7_out_5), .in_3(dabble_7_out_6), .in_4(dabble_7_out_7),
    .out_5(out_3[1]), .out_6(out_3[2]), .out_7(out_3[3]), .out_8(out_2[0]));
  Dabble dabble_7 (
    .in_1(dabble_2_out_8), .in_2(dabble_3_out_8), .in_3(dabble_1_out_8), .in_4(1'b0), .out_5(dabble_7_out_5),
    .out_6(dabble_7_out_6), .out_7(dabble_7_out_7), .out_8(out_2[1]));

  assign out_2[3:2] = 2'b00;
  assign out_4[0] = in_1[0];
endmodule

module Dabble (
  input  in_1,
  input  in_2,
  input  in_3,
  input  in_4,
  output out_5,
  output out_6,
  output out_7,
  output out_8
);

  wire comparator_1_gt;
  wire [3:0] adder_1_out;

  Adder #(.width(4)) adder_1 (.a({in_4, in_3, in_2, in_1}), .b(4'b0011), .out(adder_1_out));  // open: cin, cout
  Comparator #(.width(4), .mode("unsigned")) comparator_1 (
    .a({in_4, in_3, in_2, in_1}), .b(4'b0100), .gt(comparator_1_gt));  // open: eq, lt
  Multiplexer #(.width(4), .disabled(0)) multiplexer_1 (
    .in0({in_4, in_3, in_2, in_1}), .in1(adder_1_out), .out({out_8, out_7, out_6, out_5}),
    .sel(comparator_1_gt));  // open: en
endmodule

module _8_bit_Microprocessor (
  input  [7:0] in_1,
  output [7:0] out_2
);

  wire clock_1_out, Control_Unit_d0, Control_Unit_d1, Control_Unit_d1_2, Control_Unit_d2, Control_Unit_d2_2,
       Control_Unit_d3, Control_Unit_d3_2;
  wire [2:0] Control_Unit_f0;
  wire [3:0] Double_Dabble_2_out_2, Double_Dabble_2_out_3, Double_Dabble_2_out_4, Double_Dabble_3_out_2,
       Double_Dabble_3_out_3, Double_Dabble_3_out_4, Double_Dabble_4_out_2, Double_Dabble_4_out_3,
       Double_Dabble_4_out_4, Double_Dabble_out_2, Double_Dabble_out_3, Double_Dabble_out_4;
  wire [7:0] register_1_b, register_1_out_11, register_1_out_12, register_1_out_13, register_1_out_14;

  controlunitprobably_main Control_Unit (
    .X0_C0_C1_B0_B1_F2_F1_F0(in_1), .F0(Control_Unit_f0[0]), .F1(Control_Unit_f0[1]),
    .F2(Control_Unit_f0[2]), .D0(Control_Unit_d0), .D1(Control_Unit_d1), .D2(Control_Unit_d2),
    .D3(Control_Unit_d3), .D1_2(Control_Unit_d1_2), .D2_2(Control_Unit_d2_2), .D3_2(Control_Unit_d3_2));
  projectAUL__1__main ALU (.A(register_1_out_11), .B(register_1_b), .in_3(Control_Unit_f0), .C(out_2));
  Clock clock_1 (.out(clock_1_out));
  Register register_1 (
    .in_3(Control_Unit_d1), .in_4(Control_Unit_d2), .in_5(Control_Unit_d3), .out_11(register_1_out_11),
    .out_12(register_1_out_12), .out_13(register_1_out_13), .out_14(register_1_out_14), .Load(1'b1),
    .Clock(clock_1_out), .in_2(Control_Unit_d0), .Din(out_2), .B(register_1_b), .D1(Control_Unit_d2_2),
    .D2(Control_Unit_d3_2), .D3(Control_Unit_d1_2));
  _8_bit__7_seg_display Double_Dabble (
    .in_1(register_1_out_11), .out_2(Double_Dabble_out_2), .out_3(Double_Dabble_out_3),
    .out_4(Double_Dabble_out_4));
  _8_bit__7_seg_display Double_Dabble_2 (
    .in_1(register_1_out_14), .out_2(Double_Dabble_2_out_2), .out_3(Double_Dabble_2_out_3),
    .out_4(Double_Dabble_2_out_4));
  _8_bit__7_seg_display Double_Dabble_3 (
    .in_1(register_1_out_12), .out_2(Double_Dabble_3_out_2), .out_3(Double_Dabble_3_out_3),
    .out_4(Double_Dabble_3_out_4));
  _8_bit__7_seg_display Double_Dabble_4 (
    .in_1(register_1_out_13), .out_2(Double_Dabble_4_out_2), .out_3(Double_Dabble_4_out_3),
    .out_4(Double_Dabble_4_out_4));
  Hex_Digit_Display hex_digit_display_1 (.value(Double_Dabble_out_2));  // open: dp
  Hex_Digit_Display hex_digit_display_2 (.value(Double_Dabble_3_out_2));  // open: dp
  Hex_Digit_Display hex_digit_display_3 (.value(Double_Dabble_4_out_2));  // open: dp
  Hex_Digit_Display hex_digit_display_4 (.value(Double_Dabble_2_out_2));  // open: dp
  Hex_Digit_Display hex_digit_display_5 (.value(Double_Dabble_out_4));  // open: dp
  Hex_Digit_Display hex_digit_display_6 (.value(Double_Dabble_out_3));  // open: dp
  Hex_Digit_Display hex_digit_display_7 (.value(Double_Dabble_3_out_4));  // open: dp
  Hex_Digit_Display hex_digit_display_8 (.value(Double_Dabble_3_out_3));  // open: dp
  Hex_Digit_Display hex_digit_display_9 (.value(Double_Dabble_4_out_4));  // open: dp
  Hex_Digit_Display hex_digit_display_10 (.value(Double_Dabble_4_out_3));  // open: dp
  Hex_Digit_Display hex_digit_display_11 (.value(Double_Dabble_2_out_4));  // open: dp
  Hex_Digit_Display hex_digit_display_12 (.value(Double_Dabble_2_out_3));  // open: dp

  // Notes on the sheet:
  //                   Control Word
  //   X0 C0 C1 B0 B1 F2 F1 F0
  //   Clock
  //            Registers
  //               D0 Display
  //   D1 Display
  //   D2 Display
  //   D3 Display
endmodule

module display (
  input  [7:0] in_1
);

  wire [3:0] Double_Dabble_out_2, Double_Dabble_out_3, Double_Dabble_out_4;

  _8_bit__7_seg_display Double_Dabble (
    .in_1(in_1), .out_2(Double_Dabble_out_2), .out_3(Double_Dabble_out_3), .out_4(Double_Dabble_out_4));
  Hex_Digit_Display hex_digit_display_1 (.value(Double_Dabble_out_2));  // open: dp
  Hex_Digit_Display hex_digit_display_2 (.value(Double_Dabble_out_3));  // open: dp
  Hex_Digit_Display hex_digit_display_3 (.value(Double_Dabble_out_4));  // open: dp
endmodule
