// Logisim project projectAUL (1).circ as structural Verilog: 9 circuits, main circuit main
module main (
  input  [7:0] A,
  input  [7:0] B,
  input  [2:0] in_3,
  output [7:0] C
);

  wire and_1_out_3, and_2_out_3;
  wire [7:0] adder_1_out_3, adder_2_out_3, l_shifter_1_out, n2_multi_1_out_4, n2_multi_2_out_4,
       r_shifter_1_out;

  adder adder_1 (.in_1(A), .in_2(B), .out_3(adder_1_out_3));  // open: cOut
  \and  and_1 (.in_1(B), .in_2(A), .out_3(and_1_out_3));
  L_Shifter l_shifter_1 (.IN(B), .Out(l_shifter_1_out), ._3In(A));
  R_Shifter r_shifter_1 (.IN(B), .Out(r_shifter_1_out), ._3In(A));
  adder adder_2 (.in_1(A), .in_2(8'h1), .out_3(adder_2_out_3));  // open: cOut
  \and  and_2 (.in_1(8'h1), .in_2(A), .out_3(and_2_out_3));
  _2_Multi u_2_multi_1 (.in_2(A), .in_3({8{1'b0}}), .out_4(n2_multi_1_out_4), .in_1(and_1_out_3));
  _2_Multi u_2_multi_2 (.in_2(B), .in_3({8{1'b0}}), .out_4(n2_multi_2_out_4), .in_1(and_2_out_3));
  multiplexer multiplexer_1 (
    .in_3(adder_1_out_3), .in_4(n2_multi_1_out_4), .in_5(l_shifter_1_out), .in_6(r_shifter_1_out),
    .in_7(adder_2_out_3), .in_8(n2_multi_2_out_4), .in_9({8{1'b0}}), .in_10(B), .out_11(C), .in_1(in_3),
    .off(1'b0));
endmodule

// Adder
module adder (
  input  [7:0] in_1,
  input  [7:0] in_2,
  output [7:0] out_3,
  output cOut
);

  wire n4_adder_1_cout;

  _4_Adder u_4_adder_1 (.cIn(1'b0), .In1(in_1[3:0]), .In2(in_2[3:0]), .Out(out_3[3:0]), .cOut(n4_adder_1_cout));
  _4_Adder u_4_adder_2 (.cIn(n4_adder_1_cout), .In1(in_1[7:4]), .In2(in_2[7:4]), .Out(out_3[7:4]), .cOut(cOut));
endmodule

module _4_Adder (
  input  cIn,
  input  [3:0] In1,
  input  [3:0] In2,
  output [3:0] Out,
  output cOut
);

  wire and_1_out, and_2_out, and_3_out, and_4_out, and_5_out, and_6_out, and_7_out, and_8_out, or_1_out,
       or_2_out, or_3_out, xor_1_out, xor_2_out, xor_3_out, xor_4_out;

  and and_1 (and_1_out, In1[0], In2[0]);
  and and_2 (and_2_out, In1[1], In2[1]);
  and and_3 (and_3_out, In1[2], In2[2]);
  and and_4 (and_4_out, In1[3], In2[3]);
  xor xor_1 (xor_1_out, In1[0], In2[0]);
  and and_5 (and_5_out, cIn, xor_1_out);
  or or_1 (or_1_out, and_1_out, and_5_out);
  xor xor_2 (xor_2_out, In1[1], In2[1]);
  and and_6 (and_6_out, or_1_out, xor_2_out);
  or or_2 (or_2_out, and_2_out, and_6_out);
  xor xor_3 (xor_3_out, In1[2], In2[2]);
  and and_7 (and_7_out, or_2_out, xor_3_out);
  or or_3 (or_3_out, and_3_out, and_7_out);
  xor xor_4 (xor_4_out, In1[3], In2[3]);
  and and_8 (and_8_out, or_3_out, xor_4_out);
  or or_4 (cOut, and_4_out, and_8_out);
  xor xor_5 (Out[0], xor_1_out, cIn);
  xor xor_6 (Out[1], xor_2_out, or_1_out);
  xor xor_7 (Out[2], xor_3_out, or_2_out);
  xor xor_8 (Out[3], xor_4_out, or_3_out);
endmodule

module \and  (
  input  [7:0] in_1,
  input  [7:0] in_2,
  output out_3
);

  wire [7:0] and_1_out, and_2_out, nor_1_out, not_1_out, not_2_out;

  assign not_1_out = ~in_1;  // NOT_Gate not_1, 8 bits wide
  assign not_2_out = ~in_2;  // NOT_Gate not_2, 8 bits wide
  assign and_1_out = not_1_out & in_2;  // AND_Gate and_1, 8 bits wide
  assign and_2_out = in_1 & not_2_out;  // AND_Gate and_2, 8 bits wide
  assign nor_1_out = ~(and_1_out | and_2_out);  // NOR_Gate nor_1, 8 bits wide
  and and_3 (out_3, nor_1_out[0], nor_1_out[1], nor_1_out[2], nor_1_out[3], nor_1_out[5], nor_1_out[6], nor_1_out[7], nor_1_out[4]);
endmodule

// Multiplexer
module multiplexer (
  input  [2:0] in_1,
  input  off,
  input  [7:0] in_3,
  input  [7:0] in_4,
  input  [7:0] in_5,
  input  [7:0] in_6,
  input  [7:0] in_7,
  input  [7:0] in_8,
  input  [7:0] in_9,
  input  [7:0] in_10,
  output [7:0] out_11
);

  wire [7:0] and_1_out, and_2_out, and_3_out, and_4_out, and_5_out, and_6_out, and_7_out, and_8_out,
       not_1_out, not_2_out, not_3_out, not_4_out;

  assign not_1_out = ~{8{in_1[2]}};  // NOT_Gate not_1, 8 bits wide
  assign not_2_out = ~{8{in_1[1]}};  // NOT_Gate not_2, 8 bits wide
  assign not_3_out = ~{8{in_1[0]}};  // NOT_Gate not_3, 8 bits wide
  assign not_4_out = ~{8{off}};  // NOT_Gate not_4, 8 bits wide
  assign and_1_out = not_1_out & not_3_out & not_4_out & not_2_out & in_3;  // AND_Gate and_1, 8 bits wide
  assign and_2_out = {8{in_1[0]}} & not_2_out & not_4_out & not_1_out & in_4;  // AND_Gate and_2, 8 bits wide
  assign and_3_out = not_3_out & {8{in_1[1]}} & not_4_out & not_1_out & in_5;  // AND_Gate and_3, 8 bits wide
  assign and_4_out = {8{in_1[0]}} & {8{in_1[1]}} & not_4_out & not_1_out & in_6;  // AND_Gate and_4, 8 bits wide
  assign and_5_out = not_3_out & not_2_out & not_4_out & {8{in_1[2]}} & in_7;  // AND_Gate and_5, 8 bits wide
  assign and_6_out = {8{in_1[0]}} & not_2_out & not_4_out & {8{in_1[2]}} & in_8;  // AND_Gate and_6, 8 bits wide
  assign and_7_out = not_3_out & {8{in_1[1]}} & not_4_out & {8{in_1[2]}} & in_9;  // AND_Gate and_7, 8 bits wide
  assign and_8_out = {8{in_1[0]}} & {8{in_1[1]}} & not_4_out & {8{in_1[2]}} & in_10;  // AND_Gate and_8, 8 bits wide
  ExactlyOne xor_1[7:0] (
    .out(out_11), .in0(and_1_out), .in1(and_2_out), .in2(and_3_out), .in3(and_4_out), .in4(and_5_out),
    .in5(and_6_out), .in6(and_7_out), .in7(and_8_out));
endmodule

// multi
module _2_Multi (
  input  in_1,
  input  [7:0] in_2,
  input  [7:0] in_3,
  output [7:0] out_4
);

  wire [7:0] and_1_out, and_2_out, not_1_out;

  assign not_1_out = ~{8{in_1}};  // NOT_Gate not_1, 8 bits wide
  assign and_1_out = {8{in_1}} & in_2;  // AND_Gate and_1, 8 bits wide
  assign and_2_out = not_1_out & in_3;  // AND_Gate and_2, 8 bits wide
  assign out_4 = and_1_out ^ and_2_out;  // XOR_Gate xor_1, 8 bits wide
endmodule

module L_Shifter (
  input  [7:0] IN,
  input  [7:0] _3In,
  output [7:0] Out
);

  wire or_1_out;

  or or_1 (or_1_out, _3In[7], _3In[6], _3In[5], _3In[4], _3In[3]);
  multiplexer multiplexer_1 (
    .in_3(IN), .in_4({IN[6:0], 1'b0}), .in_5({IN[5:0], 2'b00}), .in_6({IN[4:0], 3'b000}),
    .in_7({IN[3:0], 4'b0000}), .in_8({IN[2:0], {5{1'b0}}}), .in_9({IN[1:0], {6{1'b0}}}),
    .in_10({IN[0], {7{1'b0}}}), .out_11(Out), .in_1(_3In[2:0]), .off(or_1_out));
endmodule

module R_Shifter (
  input  [7:0] IN,
  input  [7:0] _3In,
  output [7:0] Out
);

  wire or_1_out;

  or or_1 (or_1_out, _3In[7], _3In[6], _3In[5], _3In[4], _3In[3]);
  multiplexer multiplexer_1 (
    .in_3(IN), .in_4({1'b0, IN[7:1]}), .in_5({2'b00, IN[7:2]}), .in_6({3'b000, IN[7:3]}),
    .in_7({4'b0000, IN[7:4]}), .in_8({{5{1'b0}}, IN[7:5]}), .in_9({{6{1'b0}}, IN[7:6]}),
    .in_10({{7{1'b0}}, IN[7]}), .out_11(Out), .in_1(_3In[2:0]), .off(or_1_out));
endmodule

module shifter (
  input  in_1,
  input  [7:0] IN,
  input  [2:0] _3In,
  output [7:0] _101,
  output [7:0] _001,
  output [7:0] _011,
  output [7:0] _110,
  output [7:0] _100,
  output [7:0] _111,
  output [7:0] _000,
  output [7:0] _010,
  output [7:0] Out
);

  multiplexer multiplexer_1 (
    .in_3(IN), .in_4({in_1, IN[7:1]}), .in_5({{2{in_1}}, IN[7:2]}), .in_6({{3{in_1}}, IN[7:3]}),
    .in_7({{4{in_1}}, IN[7:4]}), .in_8({{5{in_1}}, IN[7:5]}), .in_9({{6{in_1}}, IN[7:6]}),
    .in_10({{7{in_1}}, IN[7]}), .out_11(Out), .in_1(_3In));  // open: off

  assign _000 = IN;
  assign _001 = {in_1, IN[7:1]};
  assign _010 = {{2{in_1}}, IN[7:2]};
  assign _011 = {{3{in_1}}, IN[7:3]};
  assign _100 = {{4{in_1}}, IN[7:4]};
  assign _101 = {{5{in_1}}, IN[7:5]};
  assign _110 = {{6{in_1}}, IN[7:6]};
  assign _111 = {{7{in_1}}, IN[7]};
endmodule
